# Fritzing sketch wiring_instructions (saved by Fritzing 1.0.1rc)

parts:
  M1 = WeMos D1 Mini V4.0.0
  DS2 = DS18B20 1-Wire Temperature Sensor [part_number=DS18B20]
  VCC1 = 3x AA Battery
  J1 = female pin header, 3 pins [form="♀ (female)"]

nets:
  N1: M1.RST, J1.pin3
  N2: M1.16, J1.pin1
  N3: M1.14/SCK, DS2.GND
  N4: M1.12/MISO, DS2.DQ
  N5: M1.13/MOSI, DS2.VDD
  N6: M1.GND, VCC1.-
  N7: M1.VBUS, VCC1.+

notes:
  The DS18B20 goes flat side down
  This is a 3 pin female header (I cut down a larger strip) with a jumper wire installed (not pictured)

custom parts:
  WeMos D1 Mini V4.0.0: The D1 mini is a mini wifi board based on ESP-8266EX.
  3x AA Battery: Your standard 3x AA battery pack (4.5 Volts)
